# Fritzing sketch hardware_diagram (saved by Fritzing 0.9.3b)

parts:
  LED2 = LED - 5mm [color="Orange (605nm)" package="5 mm [THT]"]
  LED3 = LED - 5mm [color="Orange (605nm)" package="5 mm [THT]"]
  LED4 = LED - 5mm [color="Orange (605nm)" package="5 mm [THT]"]
  LED5 = LED - 5mm [color="Orange (605nm)" package="5 mm [THT]"]
  Part2 = Adafruit Feather 32u4 Bluefruit [part_number="Adafruit #2829"]
  S2 = Pushbutton [package=THT]
  R1 = Resistor [tolerance=±5% resistance=10k package=THT]
  S3 = Pushbutton [package=THT]
  S4 = Pushbutton [package=THT]
  S5 = Pushbutton [package=THT]
  R2 = Resistor [tolerance=±5% resistance=10k package=THT]
  R3 = Resistor [tolerance=±5% resistance=10k package=THT]
  R4 = Resistor [tolerance=±5% resistance=10k package=THT]
  R5 = Rotary Potentiometer (Small) [maximum_resistance=100kΩ package=THT]
  S6 = Illuminated Toggle Switch [part_number=100-SP-X-T1-0-0-B1-M1 package=THT]
  LED6 = LED - 5mm [color="Red (633nm)" package="5 mm [THT]"]

nets:
  N1: LED2.cathode, Part2.12
  N2: LED2.anode, LED3.anode, LED4.anode, LED5.anode, Part2.GND, R1.Pin_0, R2.Pin_0, LED6.anode
  N3: LED3.cathode, Part2.11
  N4: LED4.cathode, Part2.10
  N5: LED5.cathode, Part2.13
  N6: Part2.A4, R5.wiper
  N7: Part2.A3, S3.leg0, R4.Pin_1
  N8: Part2.A0, S2.leg0, R1.Pin_1
  N9: Part2.EN, S6.+
  N10: S2.leg1, S3.leg1, S4.leg1, S5.leg1, R5.leg2, LED6.cathode
  N11: S4.leg0, R2.Pin_1
  N12: S5.leg0, R3.Pin_1
  N13: R3.Pin_0, R4.Pin_0, R5.leg1, S6.Ground

custom parts:
  Adafruit Feather 32u4 Bluefruit: This is the Adafruit Feather 32u4 Bluefruit - our take on an 'all-in-one' Arduino-compatible + Bluetooth Low Energy with built in USB and battery charging. Its an Adafruit Feather 32u4 with a BTLE module, ready to rock! We have other boards in the Feather family, check'em out here. Bluetooth Low Energy is the hottest new low-power, 2.4GHz spectrum wireless protocol. In particular, its the only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
  Illuminated Toggle Switch: Toggle switch with LED
